// Logisim project chirag1.circ as structural Verilog: 5 circuits, main circuit counter_div_10
module counter_div_10 (
  input  in_1,
  input  in_2,
  output Q4,
  output Q3,
  output Q2,
  output Q1
);

  wire and_1_out, and_2_out, and_3_out, and_4_out;

  and and_1 (and_1_out, in_1, in_2);
  J_K_Flip_Flop j_k_ff_1 (.J(1'b1), .clk(and_1_out), .K(1'b1), .Q(Q4), .reset(and_4_out));  // open: Qn, preset, en
  and and_2 (and_2_out, Q4, Q3);
  J_K_Flip_Flop j_k_ff_2 (.J(Q4), .clk(and_1_out), .K(Q4), .Q(Q3), .reset(and_4_out));  // open: Qn, preset, en
  J_K_Flip_Flop j_k_ff_3 (
    .J(and_2_out), .clk(and_1_out), .K(and_2_out), .Q(Q2), .reset(and_4_out));  // open: Qn, preset, en
  and and_3 (and_3_out, and_2_out, Q2);
  J_K_Flip_Flop j_k_ff_4 (
    .J(and_3_out), .clk(and_1_out), .K(and_3_out), .Q(Q1), .reset(and_4_out));  // open: Qn, preset, en
  and and_4 (and_4_out, Q1, Q3);
endmodule

module counter_div_6 (
  input  in_1,
  input  in_2,
  output Q4,
  output Q3,
  output Q2,
  output Q1
);

  wire and_1_out, and_2_out, and_3_out, and_4_out;

  and and_1 (and_1_out, in_1, in_2);
  J_K_Flip_Flop j_k_ff_1 (.J(1'b1), .clk(and_1_out), .K(1'b1), .Q(Q4), .reset(and_4_out));  // open: Qn, preset, en
  and and_2 (and_2_out, Q4, Q3);
  J_K_Flip_Flop j_k_ff_2 (.J(Q4), .clk(and_1_out), .K(Q4), .Q(Q3), .reset(and_4_out));  // open: Qn, preset, en
  J_K_Flip_Flop j_k_ff_3 (
    .J(and_2_out), .clk(and_1_out), .K(and_2_out), .Q(Q2), .reset(and_4_out));  // open: Qn, preset, en
  and and_3 (and_3_out, and_2_out, Q2);
  J_K_Flip_Flop j_k_ff_4 (
    .J(and_3_out), .clk(and_1_out), .K(and_3_out), .Q(Q1), .reset(and_4_out));  // open: Qn, preset, en
  and and_4 (and_4_out, Q2, Q3);
endmodule

module colck_chip (
  output [3:0] out_1,
  output [3:0] out_2
);

  wire and_1_out, and_2_out, and_3_out, and_4_out, and_5_out, and_6_out, clock_1_out, or_1_out;
  wire [1:0] counter_div_2_1_q2;
  wire [3:0] counter_div_6_1_q4, counter_div_10_1_q4, counter_div_input_1_q4;

  or or_1 (or_1_out, and_2_out, and_1_out);
  Clock clock_1 (.out(clock_1_out));
  counter_div_2 counter_div_2_1 (
    .in_1(clock_1_out), .in_2(or_1_out), .Q2(counter_div_2_1_q2[0]), .Q1(counter_div_2_1_q2[1]));
  and and_1 (and_1_out, counter_div_input_1_q4[3], counter_div_input_1_q4[1]);
  Hex_Digit_Display hex_digit_display_1 (.value({2'b00, counter_div_2_1_q2}));  // open: dp
  Hex_Digit_Display hex_digit_display_2 (.value(counter_div_input_1_q4));  // open: dp
  LED led_1 (.in(1'b1));
  LED led_2 (.in(1'b1));
  counter_div_input counter_div_input_1 (
    .in_2(clock_1_out), .in_3(and_3_out), .Q4(counter_div_input_1_q4[0]), .Q3(counter_div_input_1_q4[1]),
    .Q2(counter_div_input_1_q4[2]), .Q1(counter_div_input_1_q4[3]), .in_1(and_2_out));
  and and_2 (and_2_out, counter_div_2_1_q2[1], counter_div_input_1_q4[2]);
  and and_3 (and_3_out, counter_div_6_1_q4[2], counter_div_6_1_q4[1]);
  counter_div_6 counter_div_6_1 (
    .in_1(clock_1_out), .in_2(and_4_out), .Q4(counter_div_6_1_q4[0]), .Q3(counter_div_6_1_q4[1]),
    .Q2(counter_div_6_1_q4[2]), .Q1(counter_div_6_1_q4[3]));
  Hex_Digit_Display hex_digit_display_3 (.value(counter_div_6_1_q4));  // open: dp
  Hex_Digit_Display hex_digit_display_4 (.value(counter_div_10_1_q4));  // open: dp
  and and_4 (and_4_out, counter_div_10_1_q4[3], counter_div_10_1_q4[1]);
  LED led_3 (.in(1'b1));
  LED led_4 (.in(1'b1));
  Hex_Digit_Display hex_digit_display_5 (.value(out_1));  // open: dp
  counter_div_10 counter_div_10_1 (
    .in_1(clock_1_out), .in_2(and_5_out), .Q4(counter_div_10_1_q4[0]), .Q3(counter_div_10_1_q4[1]),
    .Q2(counter_div_10_1_q4[2]), .Q1(counter_div_10_1_q4[3]));
  and and_5 (and_5_out, out_1[2], out_1[1]);
  Hex_Digit_Display hex_digit_display_6 (.value(out_2));  // open: dp
  counter_div_6 counter_div_6_2 (
    .in_1(clock_1_out), .in_2(and_6_out), .Q4(out_1[0]), .Q3(out_1[1]), .Q2(out_1[2]), .Q1(out_1[3]));
  and and_6 (and_6_out, out_2[1], out_2[3]);
  counter_div_10 counter_div_10_2 (
    .in_1(clock_1_out), .in_2(1'b1), .Q4(out_2[0]), .Q3(out_2[1]), .Q2(out_2[2]), .Q1(out_2[3]));
endmodule

module counter_div_2 (
  input  in_1,
  input  in_2,
  output Q2,
  output Q1
);

  wire and_1_out, and_2_out;

  and and_1 (and_1_out, in_1, in_2);
  J_K_Flip_Flop j_k_ff_1 (.J(1'b1), .clk(and_1_out), .K(1'b1), .Q(Q2), .reset(and_2_out));  // open: Qn, preset, en
  J_K_Flip_Flop j_k_ff_2 (.J(Q2), .clk(and_1_out), .K(Q2), .Q(Q1), .reset(and_2_out));  // open: Qn, preset, en
  and and_2 (and_2_out, Q2, Q1);
endmodule

module counter_div_input (
  input  in_1,
  input  in_2,
  input  in_3,
  output Q4,
  output Q3,
  output Q2,
  output Q1
);

  wire and_1_out, and_2_out, and_3_out, and_4_out, or_1_out;

  J_K_Flip_Flop j_k_ff_1 (.J(1'b1), .clk(and_1_out), .K(1'b1), .Q(Q4), .reset(or_1_out));  // open: Qn, preset, en
  and and_1 (and_1_out, in_2, in_3);
  J_K_Flip_Flop j_k_ff_2 (.J(Q4), .clk(and_1_out), .K(Q4), .Q(Q3), .reset(or_1_out));  // open: Qn, preset, en
  and and_2 (and_2_out, Q4, Q3);
  and and_3 (and_3_out, and_2_out, Q2);
  J_K_Flip_Flop j_k_ff_3 (
    .J(and_2_out), .clk(and_1_out), .K(and_2_out), .Q(Q2), .reset(or_1_out));  // open: Qn, preset, en
  J_K_Flip_Flop j_k_ff_4 (
    .J(and_3_out), .clk(and_1_out), .K(and_3_out), .Q(Q1), .reset(or_1_out));  // open: Qn, preset, en
  or or_1 (or_1_out, and_4_out, in_1);
  and and_4 (and_4_out, Q3, Q1);
endmodule
